# Fritzing sketch sketch (saved by Fritzing 0.7.12b)
breadboards: 1

parts:
  RaspberryPi1 = Raspberry Pi Model B  # not connected
  Pi1 = Adafruit Pi Cobbler
  J1 = Basic Servo
  VCC1 = 4 x AAA Battery Mount

nets:
  N1: Pi1.5V0, J1.vcc, VCC1.+
  GND: Pi1.GND, J1.gnd, VCC1.-
  N2: Pi1.#18, J1.pulse

custom parts:
  Raspberry Pi Model B: Raspberry Pi (Model B)
  Adafruit Pi Cobbler: Adafruit Pi Cobbler GPIO Breakout for Raspberry Pi
